// Logisim project m1_37069.circ as structural Verilog: 12 circuits, main circuit main
module main (
  input  x,
  input  y,
  input  CIN,
  output SUM,
  output CARRY
);
endmodule

module NOT_NOR (
  input  x,
  output xNOT
);

  Pull_Resistor pull_resistor_1 (.node(xNOT));
  Transistor transistor_1 (.in(1'b1), .out(xNOT), .gate(x));
endmodule

module NOR_T (
  input  x,
  input  y,
  output xNORy
);

  wire transistor_1_out;

  Transistor transistor_1 (.in(1'b1), .out(transistor_1_out), .gate(x));
  Pull_Resistor pull_resistor_1 (.node(xNORy));
  Transistor transistor_2 (.in(transistor_1_out), .out(xNORy), .gate(y));
endmodule

module AND_NOR (
  input  x,
  input  y,
  output xANDy
);

  wire not_nor_1_xnot, not_nor_2_xnot, transistor_1_out;

  NOT_NOR not_nor_1 (.x(x), .xNOT(not_nor_1_xnot));
  Transistor transistor_1 (.in(1'b1), .out(transistor_1_out), .gate(not_nor_1_xnot));
  NOT_NOR not_nor_2 (.x(y), .xNOT(not_nor_2_xnot));
  Transistor transistor_2 (.in(transistor_1_out), .out(xANDy), .gate(not_nor_2_xnot));
  Pull_Resistor pull_resistor_1 (.node(xANDy));
endmodule

module OR_NOR (
  input  x,
  input  y,
  output xNORy
);

  wire pull_resistor_1_node, transistor_1_out;

  Transistor transistor_1 (.in(1'b1), .out(transistor_1_out), .gate(x));
  Pull_Resistor pull_resistor_1 (.node(pull_resistor_1_node));
  Transistor transistor_2 (.in(transistor_1_out), .out(pull_resistor_1_node), .gate(y));
  NOT_NOR not_nor_1 (.x(pull_resistor_1_node), .xNOT(xNORy));
endmodule

module XOR_SOP (
  input  x,
  input  y,
  output xXORy
);

  wire not_nor_1_xnot, not_nor_2_xnot, transistor_1_out, transistor_2_out, transistor_3_out, transistor_4_out;

  NOT_NOR not_nor_1 (.x(x), .xNOT(not_nor_1_xnot));
  Transistor transistor_1 (.in(1'b1), .out(transistor_1_out), .gate(not_nor_1_xnot));
  Transistor transistor_2 (.in(1'b1), .out(transistor_2_out), .gate(x));
  Transistor transistor_3 (.in(transistor_1_out), .out(transistor_3_out), .gate(y));
  NOT_NOR not_nor_2 (.x(y), .xNOT(not_nor_2_xnot));
  Transistor transistor_4 (.in(transistor_2_out), .out(transistor_4_out), .gate(not_nor_2_xnot));
  Pull_Resistor pull_resistor_1 (.node(transistor_3_out));
  Pull_Resistor pull_resistor_2 (.node(transistor_4_out));
  OR_NOR or_nor_1 (.x(transistor_4_out), .y(transistor_3_out), .xNORy(xXORy));
endmodule

module MAJ3 (
  input  x,
  input  y,
  input  z,
  output MAJxyz
);

  wire and_1_out, and_2_out, and_3_out, and_4_out, not_1_out, not_2_out, not_3_out;

  not not_1 (not_1_out, x);
  not not_2 (not_2_out, y);
  not not_3 (not_3_out, z);
  and and_1 (and_1_out, z, y, not_1_out);
  and and_2 (and_2_out, z, not_2_out, x);
  and and_3 (and_3_out, not_3_out, y, x);
  and and_4 (and_4_out, z, y, x);
  or or_1 (MAJxyz, and_1_out, and_2_out, and_3_out, and_4_out);
endmodule

module ODD3 (
  input  x,
  input  y,
  input  z,
  output ODDxyz
);

  wire and_1_out, and_2_out, and_3_out, and_4_out, not_1_out, not_2_out, not_3_out, not_4_out, not_5_out,
       not_6_out;

  not not_1 (not_1_out, z);
  not not_2 (not_2_out, y);
  not not_3 (not_3_out, z);
  not not_4 (not_4_out, x);
  not not_5 (not_5_out, y);
  not not_6 (not_6_out, x);
  and and_1 (and_1_out, not_1_out, not_2_out, x);
  and and_2 (and_2_out, not_3_out, y, not_4_out);
  and and_3 (and_3_out, z, not_5_out, not_6_out);
  and and_4 (and_4_out, z, y, x);
  or or_1 (ODDxyz, and_1_out, and_2_out, and_3_out, and_4_out);
endmodule

module PERSONAL_F (
  input  x,
  input  y,
  input  z,
  output Fxyz
);

  wire and_1_out, and_2_out, and_3_out, not_1_out, not_2_out, not_3_out;

  not not_1 (not_1_out, y);
  not not_2 (not_2_out, y);
  not not_3 (not_3_out, x);
  and and_1 (and_1_out, z, not_1_out, x);
  and and_2 (and_2_out, z, not_2_out, not_3_out);
  and and_3 (and_3_out, z, y, x);
  or or_1 (Fxyz, and_1_out, and_2_out, and_3_out);
endmodule

module HALF_ADDER (
  input  x,
  input  y,
  output SUM,
  output CARRY
);

  XOR_SOP xor_sop_1 (.x(x), .y(y), .xXORy(SUM));
  AND_NOR and_nor_1 (.x(x), .y(y), .xANDy(CARRY));
endmodule

module FULL_ADDER_A (
  input  x,
  input  y,
  input  CIN,
  output SUM,
  output COUT
);

  ODD3 odd3_1 (.x(x), .y(y), .z(CIN), .ODDxyz(SUM));
  MAJ3 maj3_1 (.x(x), .y(y), .z(CIN), .MAJxyz(COUT));
endmodule

module FULL_ADDER_B (
  input  x,
  input  y,
  input  CIN,
  output SUM,
  output COUT
);

  wire half_adder_1_carry, half_adder_1_sum, half_adder_2_carry;

  HALF_ADDER half_adder_1 (.x(x), .y(y), .SUM(half_adder_1_sum), .CARRY(half_adder_1_carry));
  HALF_ADDER half_adder_2 (.x(half_adder_1_sum), .y(CIN), .SUM(SUM), .CARRY(half_adder_2_carry));
  or or_1 (COUT, half_adder_2_carry, half_adder_1_carry);
endmodule
